# Fritzing sketch kiln_control (saved by Fritzing 0.9.3b)
stripboards: 1

parts:
  J1 = female pin header, 8 pins [form="♀ (female)"]
  J2 = female pin header, 8 pins [form="♀ (female)"]
  J3 = male pin header, 8 pins [form="♂ (male)"]
  J4 = male pin header, 8 pins [form="♂ (male)"]
  S1 = SWITCH-MOMENTARY-2 [package=tactile_switch_tall]
  R2 = Resistor [tolerance=±5% resistance=4.7k package=THT]
  U1 = mystery part, 3 pins [chip_label=AMS1117]
  U1_2 = mystery part, 3 pins [chip_label=AMS1117]
  DS1 = DS18B20 1-Wire Temperature Sensor [part_number=DS18B20]
  R3 = Resistor [tolerance=±5% resistance=4.7k package=THT]
  J8 = female pin header, 6 pins [form="♀ (female)"]
  J9 = Screw terminal - 2 pins [package=THT]
  J10 = female pin header, 18 pins [form="♀ (female)"]  # not connected
  U2 = ESP-12F (ESP8266 WiFi Module) [part_number=ESP8266]
  Bauteil1 = Adafruit Micro USB Breakout [part_number="Adafruit #1833"]

nets:
  N1: J1.pin1, J3.pin1, U2.TXD0
  N2: J1.pin2, J3.pin2, U2.RXD0
  N3: J1.pin3, J3.pin3, S1.2, R2.Pin_0, U2.GPIO5
  N4: J1.pin4, J3.pin4, DS1.DQ, R3.Pin_1, U2.GPIO4
  N5: J1.pin5, J3.pin5, U2.GPIO0
  N6: J1.pin6, J3.pin6, U2.GPIO2
  N7: J1.pin7, J3.pin7, U2.GPIO15
  GND: J1.pin8, J3.pin8, U1.pin1, U1_2.pin1, DS1.GND, J8.pin3, J9.pin2, U2.GND, Bauteil1.GND
  N8: J2.pin1, J4.pin1, U2.RST
  N9: J2.pin2, J4.pin2, U2.ADC0
  N10: J2.pin3, J4.pin3, U2.EN
  N11: J2.pin4, J4.pin4, J9.pin1, U2.GPIO16
  N12: J2.pin5, J4.pin5, J8.pin6, U2.GPIO14
  N13: J2.pin6, J4.pin6, J8.pin5, U2.GPIO12
  N14: J2.pin7, J4.pin7, J8.pin4, U2.GPIO13
  VDD: J2.pin8, J4.pin8, R2.Pin_1, U1.pin2, U1_2.pin2, DS1.VDD, R3.Pin_0, J8.pin2, U2.VCC
  N15: U1.pin3, U1_2.pin3, Bauteil1.VBUS

notes:
  GPIO14 -> CLK
  GPIO12 -> CS
  GPIO16 -> SSR
  18 Löcher
  3.3V
  GND
  DO
  CS
  CLK
  GPIO13 -> D0

custom parts:
  ESP-12F (ESP8266 WiFi Module): WiFi Module based on the ESP8266 with onboard PCB antenna and UART communications
  Adafruit Micro USB Breakout: Simple but effective - this breakout board has a USB Micro-B connector, with all 5 pins broken out. Great for pairing with a microcontroller with USB support, or adding USB 5V power to a project. We use a micro-AB connector with through-hole shielding pads for an excellent strong connection - it won't rip off by accident! Comes with one fully assembled and tested micro B breakout PCB and a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
